# Fritzing sketch led-pattern (saved by Fritzing 0.9.6b)
breadboards: 1

parts:
  Arduino_UNO_—_D2/D3/D4/D5 = Arduino Uno (Rev3)
  K(-)_A(+) = LED - 5mm [color="Blue (430nm)" package="5 mm [THT]"]
  R1 = Resistor [tolerance=±1% resistance=330 package=THT]
  K(-)_A(+)_2 = LED - 5mm [color="Red (633nm)" package="5 mm [THT]"]
  R2 = Resistor [tolerance=±1% resistance=330 package=THT]
  K(-)_A(+)_3 = LED - 5mm [color="White (4500K)" package="5 mm [THT]"]
  R3 = Resistor [tolerance=±1% resistance=330 package=THT]
  K(-)_A(+)_4 = LED - 5mm [color="Green (555nm)" package="5 mm [THT]"]
  R4 = Resistor [tolerance=±1% resistance=330 package=THT]

nets:
  N1: Arduino_UNO_—_D2/D3/D4/D5.GND, K(-)_A(+).cathode, K(-)_A(+)_2.cathode, K(-)_A(+)_3.cathode, K(-)_A(+)_4.cathode
  N2: Arduino_UNO_—_D2/D3/D4/D5.D2, R1.Pin_0
  N3: Arduino_UNO_—_D2/D3/D4/D5.D3_PWM, R2.Pin_0
  N4: Arduino_UNO_—_D2/D3/D4/D5.D4, R3.Pin_0
  N5: Arduino_UNO_—_D2/D3/D4/D5.D5_PWM, R4.Pin_0
  N6: K(-)_A(+).anode, R1.Pin_1
  N7: K(-)_A(+)_2.anode, R2.Pin_1
  N8: K(-)_A(+)_3.anode, R3.Pin_1
  N9: K(-)_A(+)_4.anode, R4.Pin_1

// code stored in the sketch: led_pattern.ino
const int ledPins[] = {2, 3, 4, 5};
const int ledCount = 4;

void setup() {
  for (int led = 0; led < ledCount; led++) {
    pinMode(ledPins[led], OUTPUT);
  }
}

void loop() {
  for (int count = 1; count <= 3; count++) {
    for (int start = 0; start < ledCount; start++) {
      for (int led = 0; led < ledCount; led++) {
        digitalWrite(ledPins[led], led >= start && led < start + count ? HIGH : LOW);
      }
      delay(500);
    }
  }
}
